// Digital circuit 4-bit-processor.dig as structural Verilog
module _4_bit_processor (
  input  clk,
  input  [1:0] IR_CTRL,
  input  [1:0] Mem_ctrl,
  input  [3:0] Mem_input,
  input  [1:0] pc_ctrl,
  output [3:0] PC_output,
  output [15:0] Instructions_16_bit,
  output [3:0] Read_data_1,
  output [3:0] Read_data_2,
  output [3:0] ALU_out
);

  wire [7:0] registerfile_write_ctrl_1_write_out;

  intr_mem_module_4_bit intr_mem_module_4_bit_1 (
    .IR_CTRL(IR_CTRL), .PC_CTRL(pc_ctrl), .intr_mem_ctrl(Mem_ctrl), .intr_mem_input(Mem_input), .clk(clk),
    .ir_output(Instructions_16_bit), .pc_output(PC_output));  // open: Mem_output
  RegisterFile_Write_ctrl registerfile_write_ctrl_1 (
    .OpCode3(Instructions_16_bit[1:0]), .write_out(registerfile_write_ctrl_1_write_out));
  // Register_file_4bit register_file_4bit_1: pin names not known; wires that end beside it: Instructions_16_bit[3:2], Instructions_16_bit[5:4], clk, ALU_out, Instructions_16_bit[1:0], registerfile_write_ctrl_1_write_out, Read_data_1, Read_data_2
  // _4_bit_ALU _4_bit_alu_1: pin names not known; wires that end beside it: Read_data_1, Read_data_2, Instructions_16_bit[8:6], ALU_out
endmodule

/* Test case Test-circuit:
IR_CTRL Mem-ctrl Mem-input pc-ctrl clk PC-output Instructions-16-bit ALU-out Read-data_1 Read-data_2
0 1 1 1 c x x x x x
0 1 2 1 c x x x x x
0 1 3 1 c x x x x x
0 1 4 1 c x x x x x
0 1 5 1 c x x x x x
0 1 6 1 c x x x x x
0 1 7 1 c x x x x x
1 0 0 1 c x x x x x
1 0 0 1 c x x x x x
1 0 0 1 c x x x x x
1 0 0 1 c x x x x x
1 0 0 1 c x x x x x
1 0 0 1 c x x x x x
1 0 0 1 c x x x x x
1 0 0 1 c x x x x x
1 0 0 1 c x x x x x
*/
