// Digital circuit 4-bit-memory.dig as structural Verilog
module _4_bit_memory (
  input  clk,
  input  [3:0] \input ,
  input  [1:0] ctrl,
  input  [3:0] Address,
  output [3:0] \output 
);

  wire and_1_out, and_2_out, and_3_out, and_4_out, and_5_out, and_6_out, and_7_out, and_8_out, and_9_out,
       and_10_out, and_11_out, and_12_out, and_13_out, and_14_out, and_15_out, and_16_out, decoder_1_out_0,
       decoder_1_out_1, decoder_1_out_2, decoder_1_out_3, decoder_1_out_4, decoder_1_out_5, decoder_1_out_6,
       decoder_1_out_7, decoder_1_out_8, decoder_1_out_9, decoder_1_out_10, decoder_1_out_11,
       decoder_1_out_12, decoder_1_out_13, decoder_1_out_14, decoder_1_out_15;
  wire [3:0] _4_bit_register_1_p4, _4_bit_register_2_p5, _4_bit_register_3_p5, _4_bit_register_4_p5,
       _4_bit_register_5_p4, _4_bit_register_6_p4, _4_bit_register_7_p4, _4_bit_register_8_p4,
       _4_bit_register_9_p4, _4_bit_register_10_p4, _4_bit_register_11_p4, _4_bit_register_12_p4,
       _4_bit_register_13_p4, _4_bit_register_14_p4, _4_bit_register_15_p4, _4_bit_register_16_p4;

  Decoder #(.Selector_Bits(4)) decoder_1 (
    .sel(Address), .out_0(decoder_1_out_0), .out_1(decoder_1_out_1), .out_2(decoder_1_out_2),
    .out_3(decoder_1_out_3), .out_4(decoder_1_out_4), .out_5(decoder_1_out_5), .out_6(decoder_1_out_6),
    .out_7(decoder_1_out_7), .out_8(decoder_1_out_8), .out_9(decoder_1_out_9), .out_10(decoder_1_out_10),
    .out_11(decoder_1_out_11), .out_12(decoder_1_out_12), .out_13(decoder_1_out_13),
    .out_14(decoder_1_out_14), .out_15(decoder_1_out_15));
  and and_1 (and_1_out, clk, decoder_1_out_0);
  and and_2 (and_2_out, clk, decoder_1_out_1);
  and and_3 (and_3_out, clk, decoder_1_out_2);
  and and_4 (and_4_out, clk, decoder_1_out_3);
  and and_5 (and_5_out, clk, decoder_1_out_4);
  and and_6 (and_6_out, clk, decoder_1_out_5);
  and and_7 (and_7_out, clk, decoder_1_out_6);
  and and_8 (and_8_out, clk, decoder_1_out_7);
  and and_9 (and_9_out, clk, decoder_1_out_8);
  and and_10 (and_10_out, clk, decoder_1_out_9);
  and and_11 (and_11_out, clk, decoder_1_out_10);
  and and_12 (and_12_out, clk, decoder_1_out_11);
  and and_13 (and_13_out, clk, decoder_1_out_12);
  and and_14 (and_14_out, clk, decoder_1_out_13);
  and and_15 (and_15_out, clk, decoder_1_out_14);
  and and_16 (and_16_out, clk, decoder_1_out_15);
  // _4_bit_Register _4_bit_register_1: pin names not known; wires that end beside it: and_1_out, \input , ctrl, _4_bit_register_1_p4
  // _4_bit_Register _4_bit_register_2: pin names not known; wires that end beside it: decoder_1_out_1, and_2_out, \input , ctrl, _4_bit_register_2_p5
  // _4_bit_Register _4_bit_register_3: pin names not known; wires that end beside it: decoder_1_out_2, and_3_out, \input , ctrl, _4_bit_register_3_p5
  // _4_bit_Register _4_bit_register_4: pin names not known; wires that end beside it: decoder_1_out_3, and_4_out, \input , ctrl, _4_bit_register_4_p5
  // _4_bit_Register _4_bit_register_5: pin names not known; wires that end beside it: and_5_out, \input , ctrl, _4_bit_register_5_p4
  // _4_bit_Register _4_bit_register_6: pin names not known; wires that end beside it: and_6_out, \input , ctrl, _4_bit_register_6_p4
  // _4_bit_Register _4_bit_register_7: pin names not known; wires that end beside it: and_7_out, \input , ctrl, _4_bit_register_7_p4
  // _4_bit_Register _4_bit_register_8: pin names not known; wires that end beside it: and_8_out, \input , ctrl, _4_bit_register_8_p4
  // _4_bit_Register _4_bit_register_9: pin names not known; wires that end beside it: and_9_out, \input , ctrl, _4_bit_register_9_p4
  // _4_bit_Register _4_bit_register_10: pin names not known; wires that end beside it: and_10_out, \input , ctrl, _4_bit_register_10_p4
  // _4_bit_Register _4_bit_register_11: pin names not known; wires that end beside it: and_11_out, \input , ctrl, _4_bit_register_11_p4
  // _4_bit_Register _4_bit_register_12: pin names not known; wires that end beside it: and_12_out, \input , ctrl, _4_bit_register_12_p4
  // _4_bit_Register _4_bit_register_13: pin names not known; wires that end beside it: and_13_out, \input , ctrl, _4_bit_register_13_p4
  // _4_bit_Register _4_bit_register_14: pin names not known; wires that end beside it: and_14_out, \input , ctrl, _4_bit_register_14_p4
  // _4_bit_Register _4_bit_register_15: pin names not known; wires that end beside it: and_15_out, \input , ctrl, _4_bit_register_15_p4
  // _4_bit_Register _4_bit_register_16: pin names not known; wires that end beside it: and_16_out, \input , ctrl, _4_bit_register_16_p4
  Multiplexer #(.Selector_Bits(4), .Bits(4)) multiplexer_1 (
    .sel(Address), .in_0(_4_bit_register_1_p4), .in_1(_4_bit_register_2_p5), .in_2(_4_bit_register_3_p5),
    .in_3(_4_bit_register_4_p5), .in_4(_4_bit_register_5_p4), .in_5(_4_bit_register_6_p4),
    .in_6(_4_bit_register_7_p4), .in_7(_4_bit_register_8_p4), .in_8(_4_bit_register_9_p4),
    .in_9(_4_bit_register_10_p4), .in_10(_4_bit_register_11_p4), .in_11(_4_bit_register_12_p4),
    .in_12(_4_bit_register_13_p4), .in_13(_4_bit_register_14_p4), .in_14(_4_bit_register_15_p4),
    .in_15(_4_bit_register_16_p4), .out(\output ));
endmodule
