// Digital circuit RegisterFile_Write_ctrl.dig as structural Verilog
module RegisterFile_Write_ctrl (
  input  [1:0] OpCode3,
  output [7:0] write_out
);

  Decoder #(.Selector_Bits(2)) decoder_1 (
    .sel(OpCode3), .out_0(write_out[0]), .out_1(write_out[2]), .out_2(write_out[4]), .out_3(write_out[6]));

  assign {write_out[7], write_out[5], write_out[3], write_out[1]} = 4'b0000;
endmodule
