// Digital circuit intr-mem-module-4-bit.dig as structural Verilog
module intr_mem_module_4_bit (
  input  [1:0] IR_CTRL,
  input  [1:0] PC_CTRL,
  input  [1:0] intr_mem_ctrl,
  input  [3:0] intr_mem_input,
  input  clk,
  output [15:0] ir_output,
  output [3:0] pc_output,
  output [3:0] Mem_output
);

  wire and_1_out, not_1_out, not_2_out;
  wire [1:0] demultiplexer_1_out_0, demultiplexer_1_out_1, demultiplexer_1_out_2, demultiplexer_1_out_3;
  wire [3:0] demultiplexer_2_out_0, demultiplexer_2_out_1, demultiplexer_2_out_2, demultiplexer_2_out_3,
       IR0_output, IR1_output, IR2_output, IR3_output;

  _4_bit_PC PC (.clk(clk), .CTRL(PC_CTRL), .\output (pc_output));
  _4_bit_memory _4_bit_memory_1 (
    .clk(clk), .\input (intr_mem_input), .ctrl(intr_mem_ctrl), .Address(pc_output), .\output (Mem_output));
  Demultiplexer #(.Selector_Bits(2), .Bits(2)) demultiplexer_1 (
    .sel(pc_output[1:0]), .in(IR_CTRL), .out_0(demultiplexer_1_out_0), .out_1(demultiplexer_1_out_1),
    .out_2(demultiplexer_1_out_2), .out_3(demultiplexer_1_out_3));
  Demultiplexer #(.Selector_Bits(2), .Bits(4)) demultiplexer_2 (
    .sel(pc_output[1:0]), .in(Mem_output), .out_0(demultiplexer_2_out_0), .out_1(demultiplexer_2_out_1),
    .out_2(demultiplexer_2_out_2), .out_3(demultiplexer_2_out_3));
  _4_bit_IR IR0 (.clk(clk), .Input(demultiplexer_2_out_0), .CTRL(demultiplexer_1_out_0), .\output (IR0_output));
  _4_bit_IR IR1 (.clk(clk), .Input(demultiplexer_2_out_1), .CTRL(demultiplexer_1_out_1), .\output (IR1_output));
  _4_bit_IR IR2 (.clk(clk), .Input(demultiplexer_2_out_2), .CTRL(demultiplexer_1_out_2), .\output (IR2_output));
  _4_bit_IR IR3 (.clk(clk), .Input(demultiplexer_2_out_3), .CTRL(demultiplexer_1_out_3), .\output (IR3_output));
  and and_1 (and_1_out, not_1_out, not_2_out);
  not not_1 (not_1_out, pc_output[0]);
  not not_2 (not_2_out, pc_output[1]);
  assign ir_output = and_1_out ? {IR3_output, IR2_output, IR1_output, IR0_output} : 16'bz;  // Driver driver_1

  // Notes on the sheet:
  //   PC_CTRL: default 1
endmodule
